// Logisim project SimpleProcessor.circ as structural Verilog: 5 circuits, main circuit main
module main (
  input  [7:0] INPT,
  input  CLOCK,
  input  RESET
);

  wire control_1_ac_we, control_1_alu_sb, control_1_pc_we, control_1_ram_we;
  wire [1:0] control_1_ac_sb, control_1_pc_sb;
  wire [4:0] control_1_adr, inc_pc_1_next_pc, PC_q;
  wire [7:0] AC_q, alu_1_result, multiplexer_1_out, ram_1_dout, rom_1_data;

  Register #(.width(5)) PC (.D(inc_pc_1_next_pc), .en(control_1_pc_we), .clk(CLOCK), .Q(PC_q), .clr(RESET));
  INC_PC inc_pc_1 (.CURR_PC(PC_q), .JUMP_ADDR(control_1_adr), .SLCT(control_1_pc_sb), .NEXT_PC(inc_pc_1_next_pc));
  ALU alu_1 (.A(AC_q), .B(ram_1_dout), .SLCT(control_1_alu_sb), .RESULT(alu_1_result));
  Register AC (.D(multiplexer_1_out), .en(control_1_ac_we), .clk(CLOCK), .Q(AC_q), .clr(RESET));
  Multiplexer #(.select(2), .width(8)) multiplexer_1 (
    .in0(INPT), .in1(ram_1_dout), .in2(alu_1_result), .out(multiplexer_1_out), .sel(control_1_ac_sb));  // open: in3
  ROM #(.addrWidth(5)) rom_1 (.addr(PC_q), .data(rom_1_data));
  RAM #(.addrWidth(5), .enables("line")) ram_1 (
    .addr(control_1_adr), .we(control_1_ram_we), .clk(CLOCK), .din(AC_q), .dout(ram_1_dout));
  CONTROL control_1 (
    .OP_ADR(rom_1_data), .AC(AC_q), .ADR(control_1_adr), .AC_WE(control_1_ac_we), .AC_SB(control_1_ac_sb),
    .PC_WE(control_1_pc_we), .PC_SB(control_1_pc_sb), .RAM_WE(control_1_ram_we), .ALU_SB(control_1_alu_sb));

  // Notes on the sheet:
  //   contents of rom_1 (hex, n*v repeats v):
  //   0 40 41 0 5f 0 9f 5f 21 60 42 61 43 62 44 63 45 64 46 65 47 66 48 67 49 e0
endmodule

module ALU (
  input  [7:0] A,
  input  [7:0] B,
  input  SLCT,
  output [7:0] RESULT
);

  wire [7:0] adder_1_out, subtractor_1_out;

  Adder adder_1 (.a(A), .b(B), .out(adder_1_out));  // open: cin, cout
  Subtractor subtractor_1 (.a(A), .b(B), .out(subtractor_1_out));  // open: bin, bout
  Multiplexer #(.width(8)) multiplexer_1 (.in0(adder_1_out), .in1(subtractor_1_out), .out(RESULT), .sel(SLCT));
endmodule

module CONTROL (
  input  [7:0] OP_ADR,
  input  [7:0] AC,
  output [4:0] ADR,
  output AC_WE,
  output [1:0] AC_SB,
  output PC_WE,
  output [1:0] PC_SB,
  output RAM_WE,
  output ALU_SB
);

  wire and_1_out, nor_1_out, skip_1_out_6;
  wire [7:0] multiplexer_1_out;

  and and_1 (and_1_out, ~nor_1_out, ~AC[7]);  // AND_Gate
  Multiplexer #(.width(8)) multiplexer_1 (.in0(8'h8), .in1(8'h18), .out(multiplexer_1_out), .sel(skip_1_out_6));
  SKIP skip_1 (.A4(OP_ADR[4]), .A3(OP_ADR[3]), .N(AC[7]), .Z(nor_1_out), .P(and_1_out), .out_6(skip_1_out_6));
  nor nor_1 (nor_1_out, AC[0], AC[1], AC[2], AC[3], AC[4], AC[5], AC[6], AC[7]);
  Multiplexer #(.select(3), .width(8)) multiplexer_2 (
    .in0(8'h9), .in1(8'hb), .in2(8'h48), .in3(8'hd), .in4(8'h8d), .in5(8'h28), .in6(multiplexer_1_out),
    .in7({8{1'b0}}), .out({ALU_SB, RAM_WE, PC_SB, PC_WE, AC_SB, AC_WE}), .sel(OP_ADR[7:5]));

  assign ADR = OP_ADR[4:0];
endmodule

module INC_PC (
  input  [4:0] CURR_PC,
  input  [4:0] JUMP_ADDR,
  input  [1:0] SLCT,
  output [4:0] NEXT_PC
);

  wire [4:0] adder_1_out, adder_2_out;

  Adder #(.width(5)) adder_1 (.a(CURR_PC), .b(5'b00001), .out(adder_1_out));  // open: cin, cout
  Adder #(.width(5)) adder_2 (.a(5'b00010), .b(CURR_PC), .out(adder_2_out));  // open: cin, cout
  Multiplexer #(.select(2), .width(5)) multiplexer_1 (
    .in0(adder_1_out), .in1(adder_2_out), .in2(JUMP_ADDR), .out(NEXT_PC), .sel(SLCT));  // open: in3
endmodule

module SKIP (
  input  A4,
  input  A3,
  input  N,
  input  Z,
  input  P,
  output out_6
);

  wire and_1_out, and_2_out, and_3_out;

  and and_1 (and_1_out, A3, Z);
  and and_2 (and_2_out, A4, P);
  and and_3 (and_3_out, N, ~A4, ~A3);  // AND_Gate
  or or_1 (out_6, and_2_out, and_1_out, and_3_out);
endmodule
